# Fritzing sketch kamf (saved by Fritzing 0.9.10b)
breadboards: 1

parts:
  Q1 = NPN-Transistor [package="TO92 [THT]"]
  Q2 = PNP-Transistor [package="TO92 [THT]"]
  R1 = Resistor [tolerance=±5% power=0.25 resistance=4.7k package=THT]
  R2 = Resistor [tolerance=±5% power=0.25 resistance=1k package=THT]
  R3 = Resistor [tolerance=±5% power=0.25 resistance=4.7k package=THT]
  R4 = Resistor [tolerance=±5% power=0.25 resistance=100 package=THT]
  Q3 = PNP-Transistor [package="TO92 [THT]"]
  Q4 = NPN-Transistor [package="TO92 [THT]"]
  R5 = Resistor [tolerance=±5% power=0.25 resistance=4.7k package=THT]
  R6 = Resistor [tolerance=±5% power=0.25 resistance=1k package=THT]
  R7 = Resistor [tolerance=±5% power=0.25 resistance=4.7k package=THT]
  R8 = Resistor [tolerance=±5% power=0.25 resistance=100 package=THT]
  IC1 = IC, DIP package, 28 pins [chip_label=W27C512]
  U1 = atmega328 [package=dip]  # not connected
  U2 = 74HC595 [package="DIP16 [THT]"]
  U3 = 74HC595 [package="DIP16 [THT]"]

nets:
  GND: Q1.E, R3.Pin_1, Q4.E
  N1: Q1.C, R1.Pin_0
  12V: Q2.E, R2.Pin_0, Q3.E, R6.Pin_0
  N2: Q2.B, R1.Pin_1, R2.Pin_1
  N3: Q2.C, R4.Pin_0
  N4: R3.Pin_0, R4.Pin_1
  N5: Q3.B, R5.Pin_1, R6.Pin_1
  N6: Q3.C, R8.Pin_0
  N7: Q4.C, R5.Pin_0
  N8: R7.Pin_0, R8.Pin_1
  N9: IC1.pin1, U3.Q7
  N10: IC1.pin2, U3.Q4
  N11: IC1.pin3, U2.Q7
  N12: IC1.pin4, U2.Q6
  N13: IC1.pin5, U2.Q5
  N14: IC1.pin6, U2.Q4
  N15: IC1.pin7, U2.Q3
  N16: IC1.pin8, U2.Q2
  N17: IC1.pin9, U2.Q1
  N18: IC1.pin10, U2.Q0
  N19: IC1.pin21, U3.Q2
  N20: IC1.pin23, U3.Q3
  N21: IC1.pin25, U3.Q0
  N22: IC1.pin26, U3.Q5
  N23: IC1.pin27, U3.Q6
  N24: U2.Q7', U3.DS
